// Logisim project 1bitALU.circ as structural Verilog: 1 circuit, main circuit main
module main (
  input  A,
  input  B,
  input  Cin,
  input  [2:0] Sel,
  output Output,
  output Co
);

  wire adder_1_out, and_1_out, or_1_out, xor_1_out;

  xor xor_1 (xor_1_out, B, Sel[2]);
  and and_1 (and_1_out, A, B);
  or or_1 (or_1_out, A, B);
  Adder #(.width(1)) adder_1 (.a(A), .b(xor_1_out), .out(adder_1_out), .cin(Cin), .cout(Co));
  Multiplexer #(.select(3)) multiplexer_1 (
    .in0(and_1_out), .in1(or_1_out), .in2(adder_1_out), .in6(adder_1_out), .in7(B), .out(Output), .sel(Sel));  // open: in3, in4, in5, en

  // Other names for the same wires on the sheet: S0 = Sel[0]; Selector[2:0] = Sel; S1 = Sel[1]; S2 = Sel[2]
endmodule
