// Logisim project 32bitSignExtender.circ as structural Verilog: 1 circuit, main circuit main
module main (
  input  [31:0] in_1,
  output [31:0] out_2
);

  wire not_1_out;

  not not_1 (not_1_out, in_1[26]);
  Multiplexer #(.width(32)) multiplexer_1 (
    .in0({{14{in_1[23]}}, in_1[22:5]}), .in1({{24{in_1[20]}}, in_1[19:12]}), .out(out_2), .sel(not_1_out));  // open: en
endmodule
