// Logisim project ALUControlv2.circ as structural Verilog: 1 circuit, main circuit main
module main (
  input  Op1,
  input  Op0,
  input  [31:0] A,
  output [3:0] out_4
);

  wire and_1_out, and_2_out, and_3_out;

  and and_1 (and_1_out, Op1, A[30], ~A[29], A[24]);  // AND_Gate
  and and_2 (and_2_out, Op1, ~A[29], A[24]);  // AND_Gate
  and and_3 (and_3_out, Op1, ~A[30], A[29], ~A[24]);  // AND_Gate
  or or_1 (out_4[2], Op0, and_1_out);
  or or_2 (out_4[1], ~Op1, and_2_out);  // OR_Gate
  or or_3 (out_4[0], Op0, and_3_out);
  and and_4 (out_4[3], ~Op1, Op1);  // AND_Gate
endmodule
