// Logisim project BiggieALU.circ as structural Verilog: 1 circuit, main circuit main
// A0
module main (
  input  in_1,
  input  [31:0] A,
  input  [31:0] B,
  input  [3:0] Selector,
  output [31:0] A_2,
  output Carry_bit,
  output Zero_Output
);

  wire main_1_co, main_2_co, main_3_co, main_4_co, main_5_co, main_6_co, main_7_co, main_8_co, main_9_co,
       main_10_co, main_11_co, main_12_co, main_13_co, main_14_co, main_15_co, main_16_co, main_17_co,
       main_18_co, main_19_co, main_20_co, main_21_co, main_22_co, main_23_co, main_24_co, main_25_co,
       main_26_co, main_27_co, main_28_co, main_29_co, main_30_co, main_31_co, not_1_out, or_1_out, or_2_out,
       Subtraction;

  not not_1 (not_1_out, Selector[0]);
  and and_1 (Subtraction, not_1_out, Selector[1], Selector[2]);
  or or_1 (or_1_out, Subtraction, in_1);
  _1bitALU_main main_1 (.A(A[0]), .B(B[0]), .Cin(or_1_out), .Sel(Selector[2:0]), .Output(A_2[0]), .Co(main_1_co));
  _1bitALU_main main_2 (.A(A[1]), .B(B[1]), .Cin(main_1_co), .Sel(Selector[2:0]), .Output(A_2[1]), .Co(main_2_co));
  _1bitALU_main main_3 (.A(A[2]), .B(B[2]), .Cin(main_2_co), .Sel(Selector[2:0]), .Output(A_2[2]), .Co(main_3_co));
  _1bitALU_main main_4 (.A(A[3]), .B(B[3]), .Cin(main_3_co), .Sel(Selector[2:0]), .Output(A_2[3]), .Co(main_4_co));
  _1bitALU_main main_5 (.A(A[4]), .B(B[4]), .Cin(main_4_co), .Sel(Selector[2:0]), .Output(A_2[4]), .Co(main_5_co));
  _1bitALU_main main_6 (.A(A[5]), .B(B[5]), .Cin(main_5_co), .Sel(Selector[2:0]), .Output(A_2[5]), .Co(main_6_co));
  _1bitALU_main main_7 (.A(A[6]), .B(B[6]), .Cin(main_6_co), .Sel(Selector[2:0]), .Output(A_2[6]), .Co(main_7_co));
  _1bitALU_main main_8 (.A(A[7]), .B(B[7]), .Cin(main_7_co), .Sel(Selector[2:0]), .Output(A_2[7]), .Co(main_8_co));
  _1bitALU_main main_9 (.A(A[8]), .B(B[8]), .Cin(main_8_co), .Sel(Selector[2:0]), .Output(A_2[8]), .Co(main_9_co));
  _1bitALU_main main_10 (.A(A[9]), .B(B[9]), .Cin(main_9_co), .Sel(Selector[2:0]), .Output(A_2[9]), .Co(main_10_co));
  _1bitALU_main main_11 (
    .A(A[10]), .B(B[10]), .Cin(main_10_co), .Sel(Selector[2:0]), .Output(A_2[10]), .Co(main_11_co));
  _1bitALU_main main_12 (
    .A(A[11]), .B(B[11]), .Cin(main_11_co), .Sel(Selector[2:0]), .Output(A_2[11]), .Co(main_12_co));
  _1bitALU_main main_13 (
    .A(A[12]), .B(B[12]), .Cin(main_12_co), .Sel(Selector[2:0]), .Output(A_2[12]), .Co(main_13_co));
  _1bitALU_main main_14 (
    .A(A[13]), .B(B[13]), .Cin(main_13_co), .Sel(Selector[2:0]), .Output(A_2[13]), .Co(main_14_co));
  _1bitALU_main main_15 (
    .A(A[14]), .B(B[14]), .Cin(main_14_co), .Sel(Selector[2:0]), .Output(A_2[14]), .Co(main_15_co));
  _1bitALU_main main_16 (
    .A(A[15]), .B(B[15]), .Cin(main_15_co), .Sel(Selector[2:0]), .Output(A_2[15]), .Co(main_16_co));
  _1bitALU_main main_17 (
    .A(A[16]), .B(B[16]), .Cin(main_16_co), .Sel(Selector[2:0]), .Output(A_2[16]), .Co(main_17_co));
  _1bitALU_main main_18 (
    .A(A[17]), .B(B[17]), .Cin(main_17_co), .Sel(Selector[2:0]), .Output(A_2[17]), .Co(main_18_co));
  _1bitALU_main main_19 (
    .A(A[18]), .B(B[18]), .Cin(main_18_co), .Sel(Selector[2:0]), .Output(A_2[18]), .Co(main_19_co));
  _1bitALU_main main_20 (
    .A(A[19]), .B(B[19]), .Cin(main_19_co), .Sel(Selector[2:0]), .Output(A_2[19]), .Co(main_20_co));
  _1bitALU_main main_21 (
    .A(A[20]), .B(B[20]), .Cin(main_20_co), .Sel(Selector[2:0]), .Output(A_2[20]), .Co(main_21_co));
  _1bitALU_main main_22 (
    .A(A[21]), .B(B[21]), .Cin(main_21_co), .Sel(Selector[2:0]), .Output(A_2[21]), .Co(main_22_co));
  _1bitALU_main main_23 (
    .A(A[22]), .B(B[22]), .Cin(main_22_co), .Sel(Selector[2:0]), .Output(A_2[22]), .Co(main_23_co));
  _1bitALU_main main_24 (
    .A(A[23]), .B(B[23]), .Cin(main_23_co), .Sel(Selector[2:0]), .Output(A_2[23]), .Co(main_24_co));
  _1bitALU_main main_25 (
    .A(A[24]), .B(B[24]), .Cin(main_24_co), .Sel(Selector[2:0]), .Output(A_2[24]), .Co(main_25_co));
  _1bitALU_main main_26 (
    .A(A[25]), .B(B[25]), .Cin(main_25_co), .Sel(Selector[2:0]), .Output(A_2[25]), .Co(main_26_co));
  _1bitALU_main main_27 (
    .A(A[26]), .B(B[26]), .Cin(main_26_co), .Sel(Selector[2:0]), .Output(A_2[26]), .Co(main_27_co));
  _1bitALU_main main_28 (
    .A(A[27]), .B(B[27]), .Cin(main_27_co), .Sel(Selector[2:0]), .Output(A_2[27]), .Co(main_28_co));
  _1bitALU_main main_29 (
    .A(A[28]), .B(B[28]), .Cin(main_28_co), .Sel(Selector[2:0]), .Output(A_2[28]), .Co(main_29_co));
  _1bitALU_main main_30 (
    .A(A[29]), .B(B[29]), .Cin(main_29_co), .Sel(Selector[2:0]), .Output(A_2[29]), .Co(main_30_co));
  _1bitALU_main main_31 (
    .A(A[30]), .B(B[30]), .Cin(main_30_co), .Sel(Selector[2:0]), .Output(A_2[30]), .Co(main_31_co));
  _1bitALU_main main_32 (.A(A[31]), .B(B[31]), .Cin(main_31_co), .Sel(Selector[2:0]), .Output(A_2[31]), .Co(Carry_bit));
  or or_2 (or_2_out, A_2[0], A_2[1], A_2[2], A_2[3], A_2[4], A_2[5], A_2[6], A_2[7], A_2[8], A_2[9], A_2[10], A_2[11], A_2[12], A_2[13], A_2[14], A_2[15], A_2[16], A_2[17], A_2[18], A_2[19], A_2[20], A_2[21], A_2[22], A_2[23], A_2[24], A_2[25], A_2[26], A_2[27], A_2[28], A_2[29], A_2[30], A_2[31]);
  not not_2 (Zero_Output, or_2_out);

  // Other names for the same wires on the sheet: O0 = A_2[0]; O1 = A_2[1]; O2 = A_2[2]; O3 = A_2[3]; O4 = A_2[4];
  //   O5 = A_2[5]; O6 = A_2[6]; O7 = A_2[7]; O8 = A_2[8]; O9 = A_2[9]; O10 = A_2[10]; O11 = A_2[11]; O12 = A_2[12];
  //   O13 = A_2[13]; O14 = A_2[14]; O15 = A_2[15]; O16 = A_2[16]; O17 = A_2[17]; O18 = A_2[18]; O19 = A_2[19];
  //   O20 = A_2[20]; O21 = A_2[21]; O22 = A_2[22]; O23 = A_2[23]; O24 = A_2[24]; O25 = A_2[25]; O26 = A_2[26];
  //   O27 = A_2[27]; O28 = A_2[28]; O29 = A_2[29]; O30 = A_2[30]; O31 = A_2[31]; S0 = Selector[0];
  //   Selector_t[2:0] = Selector[2:0]; S1 = Selector[1]; S2 = Selector[2]; S3 = Selector[3]
endmodule
