// Logisim project ForwardingUnit.circ as structural Verilog: 1 circuit, main circuit main
module main (
  input  [1:0] EX_MEM_WB,
  input  [4:0] EX_MEM_Rd,
  input  [1:0] MEM_WB_WB,
  input  [4:0] MEM_WB_Rd,
  input  [4:0] ID_EX_Rn,
  input  [4:0] ID_EX_Rm,
  output [1:0] ForwardA,
  output [1:0] ForwardB
);

  wire A01bit, A10bit, and_1_out, and_2_out, B01bit, B10bit, comparator_1_eq, comparator_2_eq,
       comparator_3_eq, comparator_4_eq;
  wire [1:0] multiplexer_1_out, multiplexer_2_out, multiplexer_3_out, multiplexer_4_out;

  and and_1 (and_1_out, EX_MEM_Rd[0], EX_MEM_Rd[1], EX_MEM_Rd[2], EX_MEM_Rd[3], EX_MEM_Rd[4]);
  and and_2 (and_2_out, MEM_WB_Rd[0], MEM_WB_Rd[1], MEM_WB_Rd[2], MEM_WB_Rd[3], MEM_WB_Rd[4]);
  Comparator #(.width(5), .mode("unsigned")) comparator_1 (
    .a(ID_EX_Rn), .b(EX_MEM_Rd), .eq(comparator_1_eq));  // open: gt, lt
  Comparator #(.width(5), .mode("unsigned")) comparator_2 (
    .a(EX_MEM_Rd), .b(ID_EX_Rm), .eq(comparator_2_eq));  // open: gt, lt
  Comparator #(.width(5), .mode("unsigned")) comparator_3 (
    .a(ID_EX_Rn), .b(MEM_WB_Rd), .eq(comparator_3_eq));  // open: gt, lt
  Comparator #(.width(5), .mode("unsigned")) comparator_4 (
    .a(MEM_WB_Rd), .b(ID_EX_Rm), .eq(comparator_4_eq));  // open: gt, lt
  and A_10 (A10bit, EX_MEM_WB[1], ~and_1_out, comparator_1_eq);  // AND_Gate
  and B_10 (B10bit, EX_MEM_WB[1], ~and_1_out, comparator_2_eq);  // AND_Gate
  and A_01 (A01bit, MEM_WB_WB[1], ~and_2_out, comparator_3_eq);  // AND_Gate
  and B_01 (B01bit, MEM_WB_WB[1], ~and_2_out, comparator_4_eq);  // AND_Gate
  Multiplexer #(.width(2)) multiplexer_1 (
    .in0(2'b00), .in1({A10bit, 1'b0}), .out(multiplexer_1_out), .sel(A10bit));  // open: en
  Multiplexer #(.width(2)) multiplexer_2 (
    .in0(2'b00), .in1({B10bit, 1'b0}), .out(multiplexer_2_out), .sel(B10bit));  // open: en
  Multiplexer #(.width(2)) multiplexer_3 (
    .in0(2'b00), .in1({1'b0, A01bit}), .out(multiplexer_3_out), .sel(A01bit));  // open: en
  Multiplexer #(.width(2)) multiplexer_4 (
    .in0(2'b00), .in1({1'b0, B01bit}), .out(multiplexer_4_out), .sel(B01bit));  // open: en
  Multiplexer #(.select(2), .width(2)) multiplexer_5 (
    .in0(2'b00), .in1(multiplexer_3_out), .in2(multiplexer_1_out), .in3(2'b01), .out(ForwardA),
    .sel({A10bit, A01bit}));  // open: en
  Multiplexer #(.select(2), .width(2)) multiplexer_6 (
    .in0(2'b00), .in1(multiplexer_4_out), .in2(multiplexer_2_out), .in3(2'b01), .out(ForwardB),
    .sel({B10bit, B01bit}));  // open: en

  // Other names for the same wires on the sheet: ASelectors[1:0] = {A10bit, A01bit};
  //   BSelectors[1:0] = {B10bit, B01bit}; EX_MEM_RegRd[4:0] = EX_MEM_Rd; MEM_WB_RegRd[4:0] = MEM_WB_Rd
endmodule
