// Logisim project FullProcessorPipelined.circ as structural Verilog: 1 circuit, main circuit main
module main (
);

  wire Clock, comparator_1_eq, main_1_if_d_write, main_1_multiplexer_selector;
  wire [1:0] EX_MEM_wb, main_1_pc_write, main_6_forwarda, main_6_forwardb, MEM_WB_wb, register_4_q;
  wire [2:0] register_5_q, register_6_q, register_14_q;
  wire [3:0] main_7_out_4;
  wire [4:0] multiplexer_3_out, register_3_q_2, register_10_q, register_11_q, register_12_q, register_17_q,
       register_19_q;
  wire [7:0] main_2_memtoreg, multiplexer_4_out;
  wire [31:0] adder_1_out, adder_2_out, main_3_out_2, main_4_out_2, main_5_read_data_1, main_5_read_data_2,
       main_8_a_2, multiplexer_1_out, multiplexer_2_out, multiplexer_5_out, multiplexer_6_out,
       multiplexer_7_out, ram_1_data, register_1_q, register_2_q, register_3_q, register_7_q, register_8_q,
       register_9_q, register_15_q, register_16_q, register_20_q, register_21_q, rom_1_data;

  Multiplexer #(.width(32)) multiplexer_1 (
    .in0(adder_1_out), .in1(adder_2_out), .out(multiplexer_1_out), .sel(main_1_pc_write[1]));  // open: en
  Clock clock_1 (.out(Clock));
  Register #(.width(32)) register_1 (
    .D(multiplexer_1_out), .en(main_1_pc_write[0]), .Q(register_1_q), .clk(Clock));  // open: clr
  Adder #(.width(32)) adder_1 (.a(register_1_q), .b(32'h4), .out(adder_1_out));  // open: cin, cout
  ROM #(.addrWidth(24), .dataWidth(32)) rom_1 (.addr(register_1_q[23:0]), .data(rom_1_data));  // open: sel
  HazardUnitv2_main main_1 (
    .ID_EX_MemRead(register_5_q), .ID_EX_Rd(register_10_q), .IF_D_Rm(register_3_q[20:16]),
    .IF_D_Rn(register_3_q_2), .Multiplexer_Selector(main_1_multiplexer_selector),
    .PC_Write(main_1_pc_write[0]), .IF_D_Write(main_1_if_d_write));
  Multiplexer #(.select(2), .width(32)) multiplexer_2 (
    .in0({register_3_q[31:10], register_3_q_2, register_3_q[4:0]}), .in1(rom_1_data), .in2({32{1'b0}}),
    .in3({32{1'b0}}), .out(multiplexer_2_out), .sel(main_1_pc_write));  // open: en
  Register #(.width(32)) register_2 (
    .D(register_1_q), .en(main_1_if_d_write), .Q(register_2_q), .clk(Clock));  // open: clr
  Register #(.width(32)) register_3 (
    .D(multiplexer_2_out), .en(main_1_if_d_write),
    .Q({register_3_q[31:10], register_3_q_2, register_3_q[4:0]}), .clk(Clock));  // open: clr
  and and_1 (main_1_pc_write[1], comparator_1_eq, main_2_memtoreg[2]);
  ProcessorControlUnit_main main_2 (
    .A({register_3_q[31:10], register_3_q_2, register_3_q[4:0]}), .ALUSrc(main_2_memtoreg[5]),
    .MemtoReg(main_2_memtoreg[0]), .RegWrite(main_2_memtoreg[1]), .MemRead(main_2_memtoreg[4]),
    .MemWrite(main_2_memtoreg[3]), .Branch(main_2_memtoreg[2]), .ALUOp0(main_2_memtoreg[6]),
    .ALUOp1(main_2_memtoreg[7]));
  Multiplexer #(.width(5)) multiplexer_3 (
    .in0(register_3_q[20:16]), .in1(register_3_q[4:0]), .out(multiplexer_3_out), .sel(register_3_q[28]));  // open: en
  Multiplexer #(.width(8)) multiplexer_4 (
    .in0(main_2_memtoreg), .in1({8{1'b0}}), .out(multiplexer_4_out), .sel(main_1_multiplexer_selector));  // open: en
  ShiftLeft2_main main_3 (.A(main_4_out_2), .out_2(main_3_out_2));
  _32bitSignExtender_main main_4 (
    .in_1({register_3_q[31:10], register_3_q_2, register_3_q[4:0]}), .out_2(main_4_out_2));
  Comparator #(.width(32)) comparator_1 (.a({32{1'b0}}), .b(main_5_read_data_2), .eq(comparator_1_eq));  // open: gt, lt
  Adder #(.width(32)) adder_2 (.a(register_2_q), .b(main_3_out_2), .out(adder_2_out));  // open: cin, cout
  RegisterFilev2_main main_5 (
    .Write(MEM_WB_wb[1]), .Write_Register(register_19_q), .Read_Register_1(register_3_q_2),
    .Read_Register_2(multiplexer_3_out), .Write_Data(multiplexer_7_out), .Read_Data_1(main_5_read_data_1),
    .Read_Data_2(main_5_read_data_2), .Clock(Clock));
  Register #(.width(2)) register_4 (.D(multiplexer_4_out[1:0]), .Q(register_4_q), .clk(Clock));  // open: en, clr
  Register #(.width(3)) register_5 (.D(multiplexer_4_out[4:2]), .Q(register_5_q), .clk(Clock));  // open: en, clr
  Register #(.width(3)) register_6 (.D(multiplexer_4_out[7:5]), .Q(register_6_q), .clk(Clock));  // open: en, clr
  Register #(.width(32)) register_7 (.D(main_5_read_data_1), .Q(register_7_q), .clk(Clock));  // open: en, clr
  Register #(.width(32)) register_8 (.D(main_5_read_data_2), .Q(register_8_q), .clk(Clock));  // open: en, clr
  Register #(.width(32)) register_9 (
    .D({register_3_q[31:10], register_3_q_2, register_3_q[4:0]}), .Q(register_9_q), .clk(Clock));  // open: en, clr
  Register #(.width(5)) register_10 (.D(register_3_q[4:0]), .Q(register_10_q), .clk(Clock));  // open: en, clr
  Register #(.width(5)) register_11 (.D(register_3_q[20:16]), .Q(register_11_q), .clk(Clock));  // open: en, clr
  Register #(.width(5)) register_12 (.D(register_3_q_2), .Q(register_12_q), .clk(Clock));  // open: en, clr
  Multiplexer #(.select(2), .width(32)) multiplexer_5 (
    .in0(register_8_q), .in1(multiplexer_7_out), .in2(register_15_q), .out(multiplexer_5_out),
    .sel(main_6_forwardb));  // open: in3, en
  Multiplexer #(.select(2), .width(32)) multiplexer_6 (
    .in0(register_7_q), .in1(multiplexer_7_out), .in2(register_15_q), .out(multiplexer_6_out),
    .sel(main_6_forwarda));  // open: in3, en
  ForwardingUnit_main main_6 (
    .EX_MEM_WB(EX_MEM_wb), .MEM_WB_WB(MEM_WB_wb), .ID_EX_Rn(register_12_q), .ID_EX_Rm(register_11_q),
    .EX_MEM_Rd(register_17_q), .MEM_WB_Rd(register_19_q), .ForwardA(main_6_forwarda),
    .ForwardB(main_6_forwardb));
  ALUControlv2_main main_7 (.Op1(register_6_q[1]), .Op0(register_6_q[2]), .A(register_9_q), .out_4(main_7_out_4));
  Register #(.width(2)) register_13 (.D(register_4_q), .Q(EX_MEM_wb), .clk(Clock));  // open: en, clr
  Register #(.width(3)) register_14 (.D(register_5_q), .Q(register_14_q), .clk(Clock));  // open: en, clr
  Register #(.width(32)) register_15 (.D(main_8_a_2), .Q(register_15_q), .clk(Clock));  // open: en, clr
  BiggieALU_main main_8 (
    .in_1(1'b0), .A(multiplexer_6_out), .B(multiplexer_5_out), .Selector(main_7_out_4), .A_2(main_8_a_2));  // open: Carry_bit, Zero_Output
  Register #(.width(32)) register_16 (.D(multiplexer_5_out), .Q(register_16_q), .clk(Clock));  // open: en, clr
  Register #(.width(5)) register_17 (.D(register_10_q), .Q(register_17_q), .clk(Clock));  // open: en, clr
  Register #(.width(2)) register_18 (.D(EX_MEM_wb), .Q(MEM_WB_wb), .clk(Clock));  // open: en, clr
  RAM #(.addrWidth(24), .dataWidth(32), .bus("separate")) ram_1 (
    .addr(register_15_q[23:0]), .din(register_16_q), .data(ram_1_data), .str(register_14_q[1]), .clk(Clock),
    .ld(register_14_q[2]));  // open: sel, clr
  Register #(.width(5)) register_19 (.D(register_17_q), .Q(register_19_q), .clk(Clock));  // open: en, clr
  Register #(.width(32)) register_20 (.D(ram_1_data), .Q(register_20_q), .clk(Clock));  // open: en, clr
  Register #(.width(32)) register_21 (.D(register_15_q), .Q(register_21_q), .clk(Clock));  // open: en, clr
  Multiplexer #(.width(32)) multiplexer_7 (
    .in0(register_21_q), .in1(register_20_q), .out(multiplexer_7_out), .sel(MEM_WB_wb[0]));  // open: en

  // Notes on the sheet:
  //   contents of rom_1 (hex, n*v repeats v):
  //   b4000061 0 0 0 8a05004c 0 0 0 aa0200cd 0 0 0 8b02004e 0 0 0 f840c024
  //   Rm
  //   Rn
  //   Rd
endmodule
