// Logisim project HazardUnitv2.circ as structural Verilog: 1 circuit, main circuit main
module main (
  input  [2:0] ID_EX_MemRead,
  input  [4:0] ID_EX_Rd,
  input  [4:0] IF_D_Rm,
  input  [4:0] IF_D_Rn,
  output Multiplexer_Selector,
  output PC_Write,
  output IF_D_Write
);

  wire comparator_1_eq, comparator_2_eq, or_1_out;

  Comparator #(.width(5)) comparator_1 (.a(ID_EX_Rd), .b(IF_D_Rm), .eq(comparator_1_eq));  // open: gt, lt
  or or_1 (or_1_out, comparator_1_eq, comparator_2_eq);
  Comparator #(.width(5)) comparator_2 (.a(ID_EX_Rd), .b(IF_D_Rn), .eq(comparator_2_eq));  // open: gt, lt
  and and_1 (Multiplexer_Selector, ID_EX_MemRead[2], or_1_out);
  not not_1 (PC_Write, Multiplexer_Selector);
  not not_2 (IF_D_Write, Multiplexer_Selector);
endmodule
