// Logisim project ProcessorControlUnit.circ as structural Verilog: 1 circuit, main circuit main
module main (
  input  [31:0] A,
  output ALUSrc,
  output MemtoReg,
  output RegWrite,
  output MemRead,
  output MemWrite,
  output Branch,
  output ALUOp0,
  output ALUOp1
);

  wire or_1_out, or_2_out, or_3_out, or_4_out, or_5_out, or_6_out, or_7_out;

  or or_1 (or_1_out, ~A[21], A[21]);  // OR_Gate
  or or_2 (or_2_out, ~A[22], A[22]);  // OR_Gate
  or or_3 (or_3_out, ~A[23], A[23]);  // OR_Gate
  or or_4 (or_4_out, ~A[24], A[24]);  // OR_Gate
  or or_5 (or_5_out, ~A[27], A[27]);  // OR_Gate
  or or_6 (or_6_out, ~A[29], A[29]);  // OR_Gate
  or or_7 (or_7_out, ~A[30], A[30]);  // OR_Gate
  and R (ALUOp0, A[31], or_7_out, or_6_out, ~A[28], or_5_out, ~A[26], A[25], or_4_out, ~A[23], ~A[22], ~A[21]);  // AND_Gate
  and LDUR (MemRead, A[31], A[30], A[29], A[28], A[27], ~A[26], ~A[25], ~A[24], ~A[23], A[22], ~A[21]);  // AND_Gate
  and STUR (MemWrite, A[31], A[30], A[29], A[28], A[27], ~A[26], ~A[25], ~A[24], ~A[23], ~A[22], ~A[21]);  // AND_Gate
  and CBZ (ALUOp1, A[31], ~A[30], A[29], A[28], ~A[27], A[26], ~A[25], ~A[24], or_3_out, or_2_out, or_1_out);  // AND_Gate
  or or_8 (ALUSrc, MemRead, MemWrite);
  or or_9 (RegWrite, ALUOp0, MemRead);

  assign Branch = ALUOp1;
  assign MemtoReg = MemRead;
endmodule
