// Logisim project RegisterFilev2.circ as structural Verilog: 1 circuit, main circuit main
module main (
  input  Write,
  input  [4:0] Write_Register,
  input  [4:0] Read_Register_1,
  input  [4:0] Read_Register_2,
  input  [31:0] Write_Data,
  input  Clock,
  output [31:0] Read_Data_1,
  output [31:0] Read_Data_2
);

  wire A0, A1, A2, A3, A4, A5, A6, A7, A8, A9, A10, A11, A12, A13, A14, A15, A16, A17, A18, A19, A20, A21,
       A22, A23, A24, A25, A26, A27, A28, A29, A30, A31, and_1_out, and_2_out, and_3_out, and_4_out,
       and_5_out, and_6_out, and_7_out, and_8_out, and_9_out, and_10_out, and_11_out, and_12_out, and_13_out,
       and_14_out, and_15_out, and_16_out, and_17_out, and_18_out, and_19_out, and_20_out, and_21_out,
       and_22_out, and_23_out, and_24_out, and_25_out, and_26_out, and_27_out, and_28_out, and_29_out,
       and_30_out, and_31_out, and_32_out;
  wire [31:0] R0, R1, R2, R3, R4, R5, R6, R7, R8, R9, R10, R11, R12, R13, R14, R15, R16, R17, R18, R19, R20,
       R21, R22, R23, R24, R25, R26, R27, R28, R29, R30, R31;

  Decoder #(.select(5)) decoder_1 (
    .out0(A0), .out1(A1), .out2(A2), .out3(A3), .out4(A4), .out5(A5), .out6(A6), .out7(A7), .out8(A8),
    .out9(A9), .out10(A10), .out11(A11), .out12(A12), .out13(A13), .out14(A14), .out15(A15), .out16(A16),
    .out17(A17), .out18(A18), .out19(A19), .out20(A20), .out21(A21), .out22(A22), .out23(A23), .out24(A24),
    .out25(A25), .out26(A26), .out27(A27), .out28(A28), .out29(A29), .out30(A30), .out31(A31),
    .sel(Write_Register));  // open: en
  and and_1 (and_1_out, A0, Write);
  and and_2 (and_2_out, A1, Write);
  and and_3 (and_3_out, A2, Write);
  and and_4 (and_4_out, A3, Write);
  and and_5 (and_5_out, A4, Write);
  and and_6 (and_6_out, A5, Write);
  and and_7 (and_7_out, A6, Write);
  and and_8 (and_8_out, A7, Write);
  and and_9 (and_9_out, A8, Write);
  and and_10 (and_10_out, A9, Write);
  and and_11 (and_11_out, A10, Write);
  and and_12 (and_12_out, A11, Write);
  and and_13 (and_13_out, A12, Write);
  and and_14 (and_14_out, A13, Write);
  and and_15 (and_15_out, A14, Write);
  and and_16 (and_16_out, A15, Write);
  Register #(.width(32), .trigger("falling")) register_1 (
    .D(Write_Data), .en(and_1_out), .Q(R0), .clk(Clock));  // open: clr
  Register #(.width(32), .trigger("falling")) register_2 (
    .D(Write_Data), .en(and_2_out), .Q(R1), .clk(Clock));  // open: clr
  Register #(.width(32), .trigger("falling")) register_3 (
    .D(Write_Data), .en(and_3_out), .Q(R2), .clk(Clock));  // open: clr
  Register #(.width(32), .trigger("falling")) register_4 (
    .D(Write_Data), .en(and_4_out), .Q(R3), .clk(Clock));  // open: clr
  Register #(.width(32), .trigger("falling")) register_5 (
    .D(Write_Data), .en(and_5_out), .Q(R4), .clk(Clock));  // open: clr
  Register #(.width(32), .trigger("falling")) register_6 (
    .D(Write_Data), .en(and_6_out), .Q(R5), .clk(Clock));  // open: clr
  Register #(.width(32), .trigger("falling")) register_7 (
    .D(Write_Data), .en(and_7_out), .Q(R6), .clk(Clock));  // open: clr
  Register #(.width(32), .trigger("falling")) register_8 (
    .D(Write_Data), .en(and_8_out), .Q(R7), .clk(Clock));  // open: clr
  Register #(.width(32), .trigger("falling")) register_9 (
    .D(Write_Data), .en(and_9_out), .Q(R8), .clk(Clock));  // open: clr
  Register #(.width(32), .trigger("falling")) register_10 (
    .D(Write_Data), .en(and_10_out), .Q(R9), .clk(Clock));  // open: clr
  Register #(.width(32), .trigger("falling")) register_11 (
    .D(Write_Data), .en(and_11_out), .Q(R10), .clk(Clock));  // open: clr
  Register #(.width(32), .trigger("falling")) register_12 (
    .D(Write_Data), .en(and_12_out), .Q(R11), .clk(Clock));  // open: clr
  Register #(.width(32), .trigger("falling")) register_13 (
    .D(Write_Data), .en(and_13_out), .Q(R12), .clk(Clock));  // open: clr
  Register #(.width(32), .trigger("falling")) register_14 (
    .D(Write_Data), .en(and_14_out), .Q(R13), .clk(Clock));  // open: clr
  Register #(.width(32), .trigger("falling")) register_15 (
    .D(Write_Data), .en(and_15_out), .Q(R14), .clk(Clock));  // open: clr
  Register #(.width(32), .trigger("falling")) register_16 (
    .D(Write_Data), .en(and_16_out), .Q(R15), .clk(Clock));  // open: clr
  and and_17 (and_17_out, A16, Write);
  and and_18 (and_18_out, A17, Write);
  and and_19 (and_19_out, A18, Write);
  and and_20 (and_20_out, A19, Write);
  and and_21 (and_21_out, A20, Write);
  and and_22 (and_22_out, A21, Write);
  and and_23 (and_23_out, A22, Write);
  and and_24 (and_24_out, A23, Write);
  and and_25 (and_25_out, A24, Write);
  and and_26 (and_26_out, A25, Write);
  and and_27 (and_27_out, A26, Write);
  and and_28 (and_28_out, A27, Write);
  and and_29 (and_29_out, A28, Write);
  and and_30 (and_30_out, A29, Write);
  and and_31 (and_31_out, A30, Write);
  and and_32 (and_32_out, A31, Write);
  Register #(.width(32), .trigger("falling")) register_17 (
    .D(Write_Data), .en(and_17_out), .Q(R16), .clk(Clock));  // open: clr
  Register #(.width(32), .trigger("falling")) register_18 (
    .D(Write_Data), .en(and_18_out), .Q(R17), .clk(Clock));  // open: clr
  Register #(.width(32), .trigger("falling")) register_19 (
    .D(Write_Data), .en(and_19_out), .Q(R18), .clk(Clock));  // open: clr
  Register #(.width(32), .trigger("falling")) register_20 (
    .D(Write_Data), .en(and_20_out), .Q(R19), .clk(Clock));  // open: clr
  Register #(.width(32), .trigger("falling")) register_21 (
    .D(Write_Data), .en(and_21_out), .Q(R20), .clk(Clock));  // open: clr
  Register #(.width(32), .trigger("falling")) register_22 (
    .D(Write_Data), .en(and_22_out), .Q(R21), .clk(Clock));  // open: clr
  Register #(.width(32), .trigger("falling")) register_23 (
    .D(Write_Data), .en(and_23_out), .Q(R22), .clk(Clock));  // open: clr
  Register #(.width(32), .trigger("falling")) register_24 (
    .D(Write_Data), .en(and_24_out), .Q(R23), .clk(Clock));  // open: clr
  Register #(.width(32), .trigger("falling")) register_25 (
    .D(Write_Data), .en(and_25_out), .Q(R24), .clk(Clock));  // open: clr
  Register #(.width(32), .trigger("falling")) register_26 (
    .D(Write_Data), .en(and_26_out), .Q(R25), .clk(Clock));  // open: clr
  Register #(.width(32), .trigger("falling")) register_27 (
    .D(Write_Data), .en(and_27_out), .Q(R26), .clk(Clock));  // open: clr
  Register #(.width(32), .trigger("falling")) register_28 (
    .D(Write_Data), .en(and_28_out), .Q(R27), .clk(Clock));  // open: clr
  Register #(.width(32), .trigger("falling")) register_29 (
    .D(Write_Data), .en(and_29_out), .Q(R28), .clk(Clock));  // open: clr
  Register #(.width(32), .trigger("falling")) register_30 (
    .D(Write_Data), .en(and_30_out), .Q(R29), .clk(Clock));  // open: clr
  Register #(.width(32), .trigger("falling")) register_31 (
    .D(Write_Data), .en(and_31_out), .Q(R30), .clk(Clock));  // open: clr
  Register #(.width(32), .trigger("falling")) register_32 (
    .D(Write_Data), .en(and_32_out), .Q(R31), .clk(Clock));  // open: clr
  Multiplexer #(.select(5), .width(32)) multiplexer_1 (
    .in0(R0), .in1(R1), .in2(R2), .in3(R3), .in4(R4), .in5(R5), .in6(R6), .in7(R7), .in8(R8), .in9(R9),
    .in10(R10), .in11(R11), .in12(R12), .in13(R13), .in14(R14), .in15(R15), .in16(R16), .in17(R17),
    .in18(R18), .in19(R19), .in20(R20), .in21(R21), .in22(R22), .in23(R23), .in24(R24), .in25(R25),
    .in26(R26), .in27(R27), .in28(R28), .in29(R29), .in30(R30), .in31(R31), .out(Read_Data_1),
    .sel(Read_Register_1));  // open: en
  Multiplexer #(.select(5), .width(32)) multiplexer_2 (
    .in0(R0), .in1(R1), .in2(R2), .in3(R3), .in4(R4), .in5(R5), .in6(R6), .in7(R7), .in8(R8), .in9(R9),
    .in10(R10), .in11(R11), .in12(R12), .in13(R13), .in14(R14), .in15(R15), .in16(R16), .in17(R17),
    .in18(R18), .in19(R19), .in20(R20), .in21(R21), .in22(R22), .in23(R23), .in24(R24), .in25(R25),
    .in26(R26), .in27(R27), .in28(R28), .in29(R29), .in30(R30), .in31(R31), .out(Read_Data_2),
    .sel(Read_Register_2));  // open: en
endmodule
