// Logisim project ShiftLeft2.circ as structural Verilog: 1 circuit, main circuit main
module main (
  input  [31:0] A,
  output [31:0] out_2
);

  and and_1 (out_2[0], ~A[30], A[30]);  // AND_Gate
  and and_2 (out_2[1], ~A[31], A[31]);  // AND_Gate

  assign out_2[31:2] = A[29:0];
endmodule
