// Logisim project tempALU.circ as structural Verilog: 1 circuit, main circuit main
module main (
  input  [31:0] in_1,
  input  [31:0] in_2,
  input  in_3,
  output out_4,
  output out_5,
  output out_6,
  output out_7
);

  wire adder_1_cout, adder_1_out, adder_2_cout, adder_2_out, adder_3_cout, adder_3_out, adder_4_cout,
       adder_4_out, and_1_out, and_2_out, and_3_out, and_4_out, or_1_out, or_2_out, or_3_out, or_4_out,
       xor_1_out, xor_2_out, xor_3_out, xor_4_out;

  xor xor_1 (xor_1_out, in_1[0], in_3);
  xor xor_2 (xor_2_out, in_3, in_1[1]);
  xor xor_3 (xor_3_out, in_1[2], in_3);
  xor xor_4 (xor_4_out, in_1[3], in_3);
  Adder #(.width(1)) adder_1 (.a(in_2[0]), .b(xor_1_out), .out(adder_1_out), .cin(in_3), .cout(adder_1_cout));
  Adder #(.width(1)) adder_2 (.a(in_2[1]), .b(xor_2_out), .out(adder_2_out), .cin(adder_1_cout), .cout(adder_2_cout));
  Adder #(.width(1)) adder_3 (.a(in_2[2]), .b(xor_3_out), .out(adder_3_out), .cin(adder_2_cout), .cout(adder_3_cout));
  Adder #(.width(1)) adder_4 (.a(in_2[3]), .b(xor_4_out), .out(adder_4_out), .cin(adder_3_cout), .cout(adder_4_cout));
  and and_1 (and_1_out, in_2[0], in_1[0]);
  or or_1 (or_1_out, in_2[0], in_1[0]);
  and and_2 (and_2_out, in_2[1], in_3);
  or or_2 (or_2_out, in_2[1], in_3);
  and and_3 (and_3_out, in_2[2], in_1[2]);
  or or_3 (or_3_out, in_2[2], in_1[2]);
  and and_4 (and_4_out, in_2[3], in_1[3]);
  or or_4 (or_4_out, in_2[3], in_1[3]);
  Multiplexer #(.select(2)) multiplexer_1 (
    .in0(adder_1_out), .in1(and_1_out), .in2(or_1_out), .in3(in_1[0]), .out(out_4));  // open: sel, en
  Multiplexer #(.select(2)) multiplexer_2 (
    .in0(adder_2_out), .in1(and_2_out), .in2(or_2_out), .in3(in_3), .out(out_5));  // open: sel, en
  Multiplexer #(.select(2)) multiplexer_3 (
    .in0(adder_3_out), .in1(and_3_out), .in2(or_3_out), .in3(in_1[2]), .out(out_6));  // open: sel, en
  Multiplexer #(.select(2)) multiplexer_4 (
    .in0(adder_4_out), .in1(and_4_out), .in2(or_4_out), .in3(in_1[3]), .out(out_7));  // open: sel, en
endmodule
